// Logisim project freq_div.circ as structural Verilog: 1 circuit, main circuit main
module main (
  input  [2:0] S,
  output Fout
);

  wire FF0_p4, FF1_p4, FF2_p4, FF3_p4, FF4_p4, FF5_p4, FF6_p4, Fin_out;

  Clock Fin (.out(Fin_out));
  // J_K_Flip_Flop #(.trigger("falling"), .NewFFLayout("true")) FF0: pin names not known; wires that end beside it: Fin_out, 1'b1, 1'b1, FF0_p4
  // J_K_Flip_Flop #(.trigger("falling"), .NewFFLayout("true")) FF1: pin names not known; wires that end beside it: FF0_p4, 1'b1, 1'b1, FF1_p4
  // J_K_Flip_Flop #(.trigger("falling"), .NewFFLayout("true")) FF2: pin names not known; wires that end beside it: FF1_p4, 1'b1, 1'b1, FF2_p4
  // J_K_Flip_Flop #(.trigger("falling"), .NewFFLayout("true")) FF3: pin names not known; wires that end beside it: FF2_p4, 1'b1, 1'b1, FF3_p4
  // J_K_Flip_Flop #(.trigger("falling"), .NewFFLayout("true")) FF4: pin names not known; wires that end beside it: FF3_p4, 1'b1, 1'b1, FF4_p4
  // J_K_Flip_Flop #(.trigger("falling"), .NewFFLayout("true")) FF5: pin names not known; wires that end beside it: FF4_p4, 1'b1, 1'b1, FF5_p4
  // J_K_Flip_Flop #(.trigger("falling"), .NewFFLayout("true")) FF6: pin names not known; wires that end beside it: FF5_p4, 1'b1, 1'b1, FF6_p4
  Multiplexer #(.select(3), .enable("false")) multiplexer_1 (
    .in0(Fin_out), .in1(FF0_p4), .in2(FF1_p4), .in3(FF2_p4), .in4(FF3_p4), .in5(FF4_p4), .in6(FF5_p4),
    .in7(FF6_p4), .out(Fout), .sel(S));

  // Notes on the sheet:
  //   Divisore di frequenza variabile: Fout = Fin / 2^S   (S = S2..S0)
  //   /1
  //   /2
  //   /4
  //   /8
  //   /16
  //   /32
  //   /64
  //   /128
endmodule
