// Logisim project registro_universale_4bit.circ as structural Verilog: 1 circuit, main circuit main
module main (
  input  Parall,
  input  P0,
  input  P1,
  input  P2,
  input  P3,
  input  DIR,
  input  D_sin,
  input  D_des,
  output Q0,
  output Q1,
  output Q2,
  output Q3
);

  wire and_1_out, and_2_out, and_3_out, and_4_out, and_5_out, and_6_out, and_7_out, and_8_out, and_9_out,
       and_10_out, and_11_out, and_12_out, and_13_out, and_14_out, Clock_out, not_1_out, not_2_out, or_1_out,
       or_2_out, or_3_out, or_4_out;

  Clock Clock (.out(Clock_out));
  not not_1 (not_1_out, DIR);
  not not_2 (not_2_out, Parall);
  and and_1 (and_1_out, not_1_out, not_2_out);
  and and_2 (and_2_out, not_2_out, DIR);
  and and_3 (and_3_out, and_1_out, D_sin);
  and and_4 (and_4_out, and_2_out, Q1);
  or or_1 (or_1_out, and_3_out, and_4_out, and_5_out);
  and and_5 (and_5_out, Parall, P0);
  D_Flip_Flop FF0 (.clk(Clock_out), .D(or_1_out), .Q(Q0));  // open: Qn, preset, reset
  and and_6 (and_6_out, and_1_out, Q0);
  and and_7 (and_7_out, and_2_out, Q2);
  or or_2 (or_2_out, and_6_out, and_7_out, and_8_out);
  and and_8 (and_8_out, Parall, P1);
  D_Flip_Flop FF1 (.clk(Clock_out), .D(or_2_out), .Q(Q1));  // open: Qn, preset, reset
  and and_9 (and_9_out, and_1_out, Q1);
  and and_10 (and_10_out, and_2_out, Q3);
  or or_3 (or_3_out, and_9_out, and_10_out, and_11_out);
  and and_11 (and_11_out, Parall, P2);
  D_Flip_Flop FF2 (.clk(Clock_out), .D(or_3_out), .Q(Q2));  // open: Qn, preset, reset
  and and_12 (and_12_out, and_1_out, Q2);
  and and_13 (and_13_out, and_2_out, D_des);
  or or_4 (or_4_out, and_12_out, and_13_out, and_14_out);
  and and_14 (and_14_out, Parall, P3);
  D_Flip_Flop FF3 (.clk(Clock_out), .D(or_4_out), .Q(Q3));  // open: Qn, preset, reset
endmodule
